// Logisim project CAN.circ as structural Verilog: 1 circuit, main circuit CAN
module CAN (
  input  Data_IN,
  input  clk,
  input  Reset,
  output [7:0] Value,
  output D_IO_CLK,
  output CS
);

  wire counter_1_carry, counter_2_carry, D_In, Shift, Write;
  wire [4:0] counter_2_q;
  wire [7:0] shift_register_1_p5;
  wire [9:0] counter_1_q;

  D_Flip_Flop d_ff_1 (.D(Data_IN), .clk(clk), .Q(D_In), .reset(Reset));  // open: Qn, preset
  Counter #(.width(10), .max('h3ff)) counter_1 (
    .clk(clk), .carry(counter_1_carry), .Q(counter_1_q));  // open: clr, load, up, count, D
  // Shift_Register shift_register_1: pin names not known; wires that end beside it: Reset, Shift, clk, D_In, shift_register_1_p5[0], shift_register_1_p5[1], shift_register_1_p5[2], shift_register_1_p5[3], shift_register_1_p5[4], shift_register_1_p5[5], shift_register_1_p5[6], shift_register_1_p5[7]
  Comparator #(.width(10), .mode("unsigned")) comparator_1 (
    .a(counter_1_q), .b(10'h200), .eq(Shift), .lt(D_IO_CLK));  // open: gt
  Counter #(.width(5), .max('h11)) counter_2 (
    .clr(Reset), .count(counter_1_carry), .clk(clk), .carry(counter_2_carry), .Q(counter_2_q));  // open: load, up, D
  Register register_1 (.D(shift_register_1_p5), .en(Write), .clk(clk), .Q(Value));  // open: clr
  and and_1 (Write, counter_1_carry, counter_2_carry);
  Comparator #(.width(5), .mode("unsigned")) comparator_2 (.a(counter_2_q), .b(5'b01010), .lt(CS));  // open: gt, eq

  // Other names for the same wires on the sheet: R = Reset

  // Notes on the sheet:
  //   Pour éviter les erreurs avec le CAN, je ne reset pas la base de temps
endmodule
