// Logisim project CPU.circ as structural Verilog: 11 circuits, main circuit main
module main (
  input  Reset,
  input  UART_INPUT,
  input  CAN_X_INPUT,
  input  CAN_Y_INPUT,
  output UART_OUTPUT,
  output SERVO_OUTPUT,
  output MOTOR_OUTPUT,
  output D_IO_CLK_X,
  output D_IO_CLK_Y,
  output CS_X,
  output CS_Y
);

  wire clk;
  wire [7:0] Addr, cpu_1_data_o, Joy_X, Joy_Y, multiplexer_1_out, NC_DOut, network_card_1_data_out,
       network_card_1_online, Time_O;
  wire [8:0] demultiplexer_1_out0, demultiplexer_1_out1, Motor_DIn, NC_DIn, Servo_DIn, Timer_DIn;
  wire [8:8] cpu_1_we;

  Clock u_clk (.out(clk));
  Multiplexer #(.select(4), .width(8), .enable("false")) multiplexer_1 (
    .in0(Time_O), .in1(NC_DOut), .in2({8{1'b0}}), .in3({8{1'b0}}), .in4(Joy_X), .in5(Joy_Y), .in6({8{1'b0}}),
    .in7({8{1'b0}}), .in8({8{1'b0}}), .in9({8{1'b0}}), .in10({8{1'b0}}), .in11({8{1'b0}}), .in12({8{1'b0}}),
    .in13({8{1'b0}}), .in14({8{1'b0}}), .in15({8{1'b0}}), .out(multiplexer_1_out), .sel(Addr[3:0]));
  Timer timer_1 (.Sleep_Time(Timer_DIn[7:0]), .EN(Timer_DIn[8]), .CLK(clk), .Reset(Reset), .TimeOut(Time_O));
  Network_Card network_card_1 (
    .Data_In(NC_DIn[7:0]), .LD_D(NC_DIn[8]), .UART_INPUT(UART_INPUT), .clk(clk), .Reset(Reset),
    .UART_OUTPUT(UART_OUTPUT), .Data_Out(network_card_1_data_out), .Online(network_card_1_online));
  // CAN Joystick_X: pin names not known; wires that end beside it: Reset, CAN_X_INPUT, clk, Joy_X, D_IO_CLK_X, CS_X
  Multiplexer #(.width(8), .enable("false")) multiplexer_2 (
    .in0(network_card_1_data_out), .in1(network_card_1_online), .out(NC_DOut), .sel(Addr[7]));
  CPU cpu_1 (
    .Reset(Reset), .clk(clk), .Data_I(multiplexer_1_out), .Addr(Addr), .WE(cpu_1_we[8]), .Data_O(cpu_1_data_o));
  Demultiplexer #(.width(9), .enable("false")) demultiplexer_1 (
    .out0(demultiplexer_1_out0), .out1(demultiplexer_1_out1), .in(Motor_DIn), .sel(Addr[7]));
  Demultiplexer #(.select(4), .width(9), .enable("false")) demultiplexer_2 (
    .out0(Timer_DIn), .out1(NC_DIn), .out2(Servo_DIn), .out3(Motor_DIn), .in({cpu_1_we[8], cpu_1_data_o}),
    .sel(Addr[3:0]));  // open: out4, out5, out6, out7, out8, out9, out10, out11, out12, out13, out14, out15
  PWM_Servo pwm_servo_1 (
    .Angle(Servo_DIn[7:0]), .EN_HT(Servo_DIn[8]), .clk(clk), .Reset(Reset), .SERVO_OUT(SERVO_OUTPUT));
  PWM_Motor pwm_motor_1 (
    .High(demultiplexer_1_out0[7:0]), .En_H(demultiplexer_1_out0[8]), .Period(demultiplexer_1_out1[7:0]),
    .En_P(demultiplexer_1_out1[8]), .clk(clk), .Reset(Reset), .MOTOR_OUT(MOTOR_OUTPUT));
  // CAN Joystick_Y: pin names not known; wires that end beside it: Reset, CAN_Y_INPUT, clk, Joy_Y, D_IO_CLK_Y, CS_Y

  // Other names for the same wires on the sheet: CSx = CS_X; CSy = CS_Y; D_CLK_X = D_IO_CLK_X; D_CLK_Y = D_IO_CLK_Y;
  //   DIN_X = CAN_X_INPUT; DIN_Y = CAN_Y_INPUT; MOUT = MOTOR_OUTPUT; R = Reset; SOUT = SERVO_OUTPUT; UIN = UART_INPUT;
  //   UOUT = UART_OUTPUT
endmodule

module CPU (
  input  Reset,
  input  clk,
  input  [7:0] Data_I,
  output [7:0] Addr,
  output WE,
  output [7:0] Data_O
);

  wire and_1_out, and_2_out, and_5_out, and_7_out, and_8_out, and_9_out, Ld, nor_1_out, or_1_out, or_2_out,
       or_3_out, Write, zncv_comp_1_ok;
  wire [1:0] and_4_out;
  wire [2:0] AddrB, AddrIn;
  wire [2:2] AddrA;
  wire [3:0] alucomplexe_1_v, InstrIn, InstrOut, OpCode, ZNCV;
  wire [7:0] adder_1_out, alucomplexe_1_sortie, DataIn, multiplexer_1_out, Parity, ValA;
  wire [7:4] multiplexer_4_out;

  and and_1 (and_1_out, OpCode[1], ~OpCode[2]);  // AND_Gate
  and and_2 (and_2_out, OpCode[0], OpCode[2]);
  or or_1 (or_1_out, and_2_out, OpCode[1]);
  or or_2 (or_2_out, OpCode[2], OpCode[0]);
  Multiplexer #(.width(8), .enable("false")) multiplexer_1 (
    .in0(Data_O), .in1({{5{1'b0}}, AddrB}), .out(multiplexer_1_out), .sel(and_1_out));
  // Probe on multiplexer_1_out
  Counter #(.width(4), .max('hf)) counter_1 (
    .clr(Reset), .load(Ld), .clk(clk), .D(InstrIn), .Q(InstrOut));  // open: up, count, carry
  nand nand_1 (Write, or_1_out, OpCode[3]);
  and and_3 (and_4_out[1], OpCode[3], or_2_out);
  and and_4 (and_4_out[0], ~OpCode[0], OpCode[3]);  // AND_Gate
  // Probe on alucomplexe_1_sortie
  AluComplexe alucomplexe_1 (
    .OP(OpCode[2:0]), .A(ValA), .B(multiplexer_1_out), .Sortie(alucomplexe_1_sortie), .V(alucomplexe_1_v[0]),
    .Negatif(alucomplexe_1_v[2]), .C(alucomplexe_1_v[1]), .Zero(alucomplexe_1_v[3]));
  Register #(.width(4)) register_1 (.D(alucomplexe_1_v), .clk(clk), .Q(ZNCV), .clr(Reset));  // open: en
  Multiplexer #(.select(2), .width(8), .enable("false")) multiplexer_2 (
    .in0(alucomplexe_1_sortie), .in1(Addr), .in2(Parity), .in3(Data_I), .out(DataIn), .sel(and_4_out));
  Banque_Registre banque_registre_1 (
    .AddrA({AddrA[2], Addr[7:6]}), .AddrB(AddrB), .En(Write), .DataIn(DataIn), .AddrIn(AddrIn), .Clk(clk),
    .Reset(Reset), .ValA(ValA), .ValB(Data_O));
  ROM_A rom_a_1 (.Addr(InstrOut), .Val({OpCode, AddrIn, AddrA[2], Addr}));
  // Probe on {OpCode, AddrIn, AddrA[2], Addr}
  Parity_C parity_c_1 (.Data(ValA), .Parity(Parity));
  and and_5 (and_5_out, ~OpCode[0], ~OpCode[1], OpCode[2], OpCode[3]);  // AND_Gate
  and and_6 (WE, OpCode[0], ~OpCode[1], OpCode[2], OpCode[3]);  // AND_Gate
  or or_3 (or_3_out, and_5_out, WE);
  Multiplexer #(.width(3), .enable("false")) multiplexer_3 (.in0(Addr[5:3]), .in1(AddrIn), .out(AddrB), .sel(or_3_out));
  nor nor_1 (nor_1_out, Addr[0], Addr[1], Addr[2], Addr[3], Addr[4], Addr[5], Addr[6], Addr[7]);
  Adder adder_1 (.a(Addr), .b({4'b0000, InstrOut}), .out(adder_1_out));  // open: cin, cout
  and and_7 (and_7_out, OpCode[0], OpCode[1], ~OpCode[2], OpCode[3]);  // AND_Gate
  and and_8 (and_8_out, ~OpCode[0], OpCode[1], ~OpCode[2], OpCode[3]);  // AND_Gate
  ZNCV_Comp zncv_comp_1 (.A(ZNCV), .B({AddrIn, AddrA[2]}), .Ok(zncv_comp_1_ok));
  Multiplexer #(.width(8), .enable("false")) multiplexer_4 (
    .in0(adder_1_out), .in1({8{1'b0}}), .out({multiplexer_4_out, InstrIn}), .sel(nor_1_out));
  and and_9 (and_9_out, and_8_out, zncv_comp_1_ok);
  or or_4 (Ld, and_7_out, and_9_out);

  // Other names for the same wires on the sheet: SeptZero[7:0] = Addr; OnzeNeuf[2:0] = AddrIn; AddrA[1:0] = Addr[7:6];
  //   Huit = AddrA[2]; R = Reset; ValB[7:0] = Data_O

  // Notes on the sheet:
  //   Un saut de 0 ramnène au début du code
endmodule

module Banque_Registre (
  input  [2:0] AddrA,
  input  [2:0] AddrB,
  input  En,
  input  [7:0] DataIn,
  input  [2:0] AddrIn,
  input  Clk,
  input  Reset,
  output [7:0] ValA,
  output [7:0] ValB
);

  wire demultiplexer_1_out0, demultiplexer_1_out1, demultiplexer_1_out2, demultiplexer_1_out3,
       demultiplexer_1_out4, demultiplexer_1_out5, demultiplexer_1_out6, demultiplexer_1_out7;
  wire [7:0] register_1_q, register_2_q, register_3_q, register_4_q, register_5_q, register_6_q,
       register_7_q, register_8_q;

  Demultiplexer #(.select(3), .enable("false")) demultiplexer_1 (
    .out0(demultiplexer_1_out0), .out1(demultiplexer_1_out1), .out2(demultiplexer_1_out2),
    .out3(demultiplexer_1_out3), .out4(demultiplexer_1_out4), .out5(demultiplexer_1_out5),
    .out6(demultiplexer_1_out6), .out7(demultiplexer_1_out7), .in(En), .sel(AddrIn));
  Register register_1 (.D(DataIn), .en(demultiplexer_1_out0), .clk(Clk), .Q(register_1_q), .clr(Reset));
  Register register_2 (.D(DataIn), .en(demultiplexer_1_out1), .clk(Clk), .Q(register_2_q), .clr(Reset));
  Register register_3 (.D(DataIn), .en(demultiplexer_1_out2), .clk(Clk), .Q(register_3_q), .clr(Reset));
  Register register_4 (.D(DataIn), .en(demultiplexer_1_out3), .clk(Clk), .Q(register_4_q), .clr(Reset));
  Register register_5 (.D(DataIn), .en(demultiplexer_1_out4), .clk(Clk), .Q(register_5_q), .clr(Reset));
  Register register_6 (.D(DataIn), .en(demultiplexer_1_out5), .clk(Clk), .Q(register_6_q), .clr(Reset));
  Register register_7 (.D(DataIn), .en(demultiplexer_1_out6), .clk(Clk), .Q(register_7_q), .clr(Reset));
  Register register_8 (.D(DataIn), .en(demultiplexer_1_out7), .clk(Clk), .Q(register_8_q), .clr(Reset));
  // Probe on register_3_q
  Multiplexer #(.select(3), .width(8), .enable("false")) multiplexer_1 (
    .in0(register_1_q), .in1(register_2_q), .in2(register_3_q), .in3(register_4_q), .in4(register_5_q),
    .in5(register_6_q), .in6(register_7_q), .in7(register_8_q), .out(ValA), .sel(AddrA));
  Multiplexer #(.select(3), .width(8), .enable("false")) multiplexer_2 (
    .in0(register_1_q), .in1(register_2_q), .in2(register_3_q), .in3(register_4_q), .in4(register_5_q),
    .in5(register_6_q), .in6(register_7_q), .in7(register_8_q), .out(ValB), .sel(AddrB));

  // Other names for the same wires on the sheet: A[2:0] = AddrA; B[2:0] = AddrB; R = Reset
endmodule

module ROM_A (
  input  [3:0] Addr,
  output [15:0] Val
);

  Multiplexer #(.select(4), .width(16), .enable("false")) multiplexer_1 (
    .in0(16'h8001), .in1(16'h2010), .in2(16'h3010), .in3(16'hb0fd), .in4(16'hda00), .in5(16'hda01),
    .in6(16'hbffc), .in7(16'hbffc), .in8(16'h1e0f), .in9({16{1'b0}}), .in10({16{1'b0}}), .in11({16{1'b0}}),
    .in12({16{1'b0}}), .in13({16{1'b0}}), .in14({16{1'b0}}), .in15({16{1'b0}}), .out(Val), .sel(Addr));
endmodule

module AluComplexe (
  input  [2:0] OP,
  input  [7:0] A,
  input  [7:0] B,
  output [7:0] Sortie,
  output V,
  output Negatif,
  output C,
  output Zero
);

  wire alusimple_1_out_5, shift_2_c;
  wire [7:0] alusimple_1_out_4, and_1_out, not_1_out, or_1_out, shift_2_result;

  // Probe on A
  // Probe on B
  // Shift shift_1: pin names not known
  AluSimple alusimple_1 (.Op(OP[0]), .A(A), .B(B), .out_4(alusimple_1_out_4), .out_5(alusimple_1_out_5), .out_6(V));
  assign not_1_out = ~A;  // NOT_Gate not_1, 8 bits wide
  Shift shift_2 (.Data(A), .Shift(B[2:0]), .Right(OP[0]), .Result(shift_2_result), .C(shift_2_c));
  assign and_1_out = A & B;  // AND_Gate and_1, 8 bits wide
  assign or_1_out = A | B;  // OR_Gate or_1, 8 bits wide
  Multiplexer #(.select(3), .width(8), .enable("false")) multiplexer_1 (
    .in0(alusimple_1_out_4), .in1(alusimple_1_out_4), .in2(shift_2_result), .in3(shift_2_result),
    .in4({{2{A[7]}}, A[6:1]}), .in5(and_1_out), .in6(or_1_out), .in7(not_1_out),
    .out({Negatif, Sortie[6:0]}), .sel(OP));
  Comparator comparator_1 (.a({Negatif, Sortie[6:0]}), .b({8{1'b0}}), .eq(Zero));  // open: gt, lt
  Multiplexer #(.select(3), .enable("false")) multiplexer_2 (
    .in0(alusimple_1_out_5), .in1(alusimple_1_out_5), .in2(shift_2_c), .in3(shift_2_c), .in4(A[0]),
    .in5(1'b0), .in6(1'b0), .in7(1'b0), .out(C), .sel(OP));

  assign Sortie[7] = Negatif;
endmodule

module Parity_C (
  input  [7:0] Data,
  output [7:0] Parity
);

  wire xor_1_out, xor_2_out, xor_3_out, xor_4_out, xor_5_out, xor_6_out;

  xor xor_1 (xor_1_out, Data[0], Data[1]);
  xor xor_2 (xor_2_out, xor_1_out, Data[2]);
  xor xor_3 (xor_3_out, xor_2_out, Data[3]);
  xor xor_4 (xor_4_out, xor_3_out, Data[4]);
  xor xor_5 (xor_5_out, xor_4_out, Data[5]);
  xor xor_6 (xor_6_out, xor_5_out, Data[6]);
  xnor xnor_1 (Parity[0], xor_6_out, Data[7]);

  assign Parity[7:1] = Data[7:1];
endmodule

module Add1bit (
  input  A,
  input  B,
  input  C_in,
  output D,
  output C_out
);

  wire and_1_out, and_2_out, and_3_out, xor_1_out;

  xor xor_1 (xor_1_out, A, B);
  and and_1 (and_1_out, A, B);
  and and_2 (and_2_out, A, C_in);
  and and_3 (and_3_out, B, C_in);
  or or_1 (C_out, and_1_out, and_2_out, and_3_out);
  xor xor_2 (D, xor_1_out, C_in);
endmodule

module Add4bits (
  input  C_in,
  input  [3:0] A,
  input  [3:0] B,
  output [3:0] D,
  output C_out
);

  wire Add1bit_1_c_out, Add1bit_2_c_out, Add1bit_3_c_out;

  Add1bit Add1bit_1 (.A(A[0]), .B(B[0]), .C_in(C_in), .D(D[0]), .C_out(Add1bit_1_c_out));
  Add1bit Add1bit_2 (.A(A[1]), .B(B[1]), .C_in(Add1bit_1_c_out), .D(D[1]), .C_out(Add1bit_2_c_out));
  Add1bit Add1bit_3 (.A(A[2]), .B(B[2]), .C_in(Add1bit_2_c_out), .D(D[2]), .C_out(Add1bit_3_c_out));
  Add1bit Add1bit_4 (.A(A[3]), .B(B[3]), .C_in(Add1bit_3_c_out), .D(D[3]), .C_out(C_out));
endmodule

module Add8bits (
  input  C_in,
  input  [7:0] A,
  input  [7:0] B,
  output [7:0] D,
  output C_out,
  output v
);

  wire Add4bits_1_c_out, and_1_out, and_2_out;

  and and_1 (and_1_out, ~A[7], ~B[7], D[7]);  // AND_Gate
  and and_2 (and_2_out, A[7], B[7], ~D[7]);  // AND_Gate
  Add4bits Add4bits_1 (.C_in(C_in), .A(A[3:0]), .B(B[3:0]), .D(D[3:0]), .C_out(Add4bits_1_c_out));
  Add4bits Add4bits_2 (.C_in(Add4bits_1_c_out), .A(A[7:4]), .B(B[7:4]), .D(D[7:4]), .C_out(C_out));
  or or_1 (v, and_1_out, and_2_out);
endmodule

module AluSimple (
  input  Op,
  input  [7:0] A,
  input  [7:0] B,
  output [7:0] out_4,
  output out_5,
  output out_6
);

  wire [7:0] multiplexer_1_out, not_1_out;

  Multiplexer #(.width(8), .enable("false")) multiplexer_1 (
    .in0(B), .in1(not_1_out), .out(multiplexer_1_out), .sel(Op));
  assign not_1_out = ~B;  // NOT_Gate not_1, 8 bits wide
  Add8bits add8bits_1 (.C_in(Op), .A(A), .B(multiplexer_1_out), .D(out_4), .C_out(out_5), .v(out_6));
endmodule

module ZNCV_Comp (
  input  [3:0] A,
  input  [3:0] B,
  output Ok
);

  wire and_1_out, and_2_out, and_3_out, and_4_out;

  and and_1 (and_1_out, A[0], B[0]);
  and and_2 (and_2_out, A[1], B[1]);
  and and_3 (and_3_out, A[2], B[2]);
  and and_4 (and_4_out, A[3], B[3]);
  or or_1 (Ok, and_1_out, and_2_out, and_3_out, and_4_out);
endmodule
