// Logisim project PWM.circ as structural Verilog: 7 circuits, main circuit PWM_Servo
module PWM_Servo (
  input  [7:0] Angle,
  input  EN_HT,
  input  clk,
  input  Reset,
  output SERVO_OUT
);

  wire [20:0] Servo_Mapper_1_out_21b;

  Servo_Mapper Servo_Mapper_1 (.In_8b(Angle), .Out_21b(Servo_Mapper_1_out_21b));
  // Probe on Servo_Mapper_1_out_21b
  PWM_Base PWM_Base_1 (
    .High_Time(Servo_Mapper_1_out_21b), .EN_HT(EN_HT), .Period(21'h1e847f), .clk(clk), .Reset(Reset),
    .PWM_OUT(SERVO_OUT));

  // Notes on the sheet:
  //   20[ms]
endmodule

module PWM_Motor (
  input  Ins,
  input  [7:0] High,
  input  En_H,
  input  clk,
  input  Reset,
  output MOTOR_OUT
);

  wire [20:0] Insane_Motor_Mapper_1_out_21b, Motor_Mapper_1_out_21b, multiplexer_1_out;

  Motor_Mapper Motor_Mapper_1 (.In_8b(High), .Out_21b(Motor_Mapper_1_out_21b));
  Insane_Motor_Mapper Insane_Motor_Mapper_1 (.In_8(High), .Out_21b(Insane_Motor_Mapper_1_out_21b));
  Multiplexer #(.width(21), .enable("false")) multiplexer_1 (
    .in0(Motor_Mapper_1_out_21b), .in1(Insane_Motor_Mapper_1_out_21b), .out(multiplexer_1_out), .sel(Ins));
  // Probe on multiplexer_1_out
  PWM_Base PWM_Base_1 (
    .High_Time(multiplexer_1_out), .EN_HT(En_H), .Period(21'h1e847f), .clk(clk), .Reset(Reset),
    .PWM_OUT(MOTOR_OUT));

  // Notes on the sheet:
  //   20[ms]
endmodule

module PWM_Base (
  input  [20:0] High_Time,
  input  EN_HT,
  input  [20:0] Period,
  input  clk,
  input  Reset,
  output PWM_OUT
);

  wire comparator_1_eq, comparator_1_gt, or_1_out;
  wire [20:0] cpt, ht;

  Register #(.width(21)) register_1 (.D(High_Time), .en(EN_HT), .clk(clk), .Q(ht), .clr(Reset));
  Comparator #(.width(21), .mode("unsigned")) comparator_1 (
    .a(cpt), .b(Period), .gt(comparator_1_gt), .eq(comparator_1_eq));  // open: lt
  Counter #(.width(21), .max('h1fffff)) counter_1 (
    .clr(or_1_out), .clk(clk), .Q(cpt));  // open: load, up, count, D, carry
  or or_1 (or_1_out, Reset, comparator_1_gt, comparator_1_eq);
  Comparator #(.width(21), .mode("unsigned")) comparator_2 (.a(cpt), .b(ht), .lt(PWM_OUT));  // open: gt, eq

  // Other names for the same wires on the sheet: p[20:0] = Period; R = Reset
endmodule

module Servo_Mapper (
  input  [7:0] In_8b,
  output [20:0] Out_21b
);

  wire comparator_1_gt, comparator_2_lt, or_1_out;
  wire [17:0] adder_1_out, multiplexer_1_out, Multiply_18bits_1_product;

  Comparator #(.mode("unsigned")) comparator_1 (.a(In_8b), .b(8'hfa), .gt(comparator_1_gt));  // open: eq, lt
  Comparator #(.mode("unsigned")) comparator_2 (.a(In_8b), .b(8'h5), .lt(comparator_2_lt));  // open: gt, eq
  Multiply_18b Multiply_18bits_1 (.A(18'h111), .B(In_8b), .Product(Multiply_18bits_1_product));
  Adder #(.width(18)) adder_1 (.a(Multiply_18bits_1_product), .b(18'h1adb0), .out(adder_1_out));  // open: cin, cout
  Multiplexer #(.width(18), .enable("false")) multiplexer_1 (
    .in0(18'h1adb0), .in1(18'h2bf20), .out(multiplexer_1_out), .sel(comparator_1_gt));
  or or_1 (or_1_out, comparator_1_gt, comparator_2_lt);
  // Probe on Out_21b[17:0]
  Multiplexer #(.width(18), .enable("false")) multiplexer_2 (
    .in0(adder_1_out), .in1(multiplexer_1_out), .out(Out_21b[17:0]), .sel(or_1_out));

  assign Out_21b[20:18] = 3'b000;
endmodule

module Motor_Mapper (
  input  [7:0] In_8b,
  output [20:0] Out_21b
);

  wire comparator_1_gt, comparator_2_lt, or_1_out;
  wire [17:0] adder_1_out, multiplexer_1_out, Multiply_18bits_1_product;

  Comparator #(.mode("unsigned")) comparator_1 (.a(In_8b), .b(8'hfa), .gt(comparator_1_gt));  // open: eq, lt
  Comparator #(.mode("unsigned")) comparator_2 (.a(In_8b), .b(8'h5), .lt(comparator_2_lt));  // open: gt, eq
  Multiply_18b Multiply_18bits_1 (.A(18'h9c), .B(In_8b), .Product(Multiply_18bits_1_product));
  Adder #(.width(18)) adder_1 (.a(Multiply_18bits_1_product), .b(18'h1fbd0), .out(adder_1_out));  // open: cin, cout
  Multiplexer #(.width(18), .enable("false")) multiplexer_1 (
    .in0(18'h1fbd0), .in1(18'h29810), .out(multiplexer_1_out), .sel(comparator_1_gt));
  or or_1 (or_1_out, comparator_1_gt, comparator_2_lt);
  Multiplexer #(.width(18), .enable("false")) multiplexer_2 (
    .in0(adder_1_out), .in1(multiplexer_1_out), .out(Out_21b[17:0]), .sel(or_1_out));
  // Probe on {3'b000, Out_21b[17:0]}

  assign Out_21b[20:18] = 3'b000;
endmodule

module Insane_Motor_Mapper (
  input  [7:0] In_8,
  output [20:0] Out_21b
);

  wire comparator_1_gt, comparator_2_lt, or_1_out;
  wire [17:0] adder_1_out, multiplexer_1_out, Multiply_18b_1_product;

  Comparator #(.mode("unsigned")) comparator_1 (.a(In_8), .b(8'hfa), .gt(comparator_1_gt));  // open: eq, lt
  Comparator #(.mode("unsigned")) comparator_2 (.a(In_8), .b(8'h5), .lt(comparator_2_lt));  // open: gt, eq
  Multiply_18b Multiply_18b_1 (.A(18'h187), .B(In_8), .Product(Multiply_18b_1_product));
  Adder #(.width(18)) adder_1 (.a(Multiply_18b_1_product), .b(18'h186a0), .out(adder_1_out));  // open: cin, cout
  Multiplexer #(.width(18), .enable("false")) multiplexer_1 (
    .in0(18'h186a0), .in1(18'h30d40), .out(multiplexer_1_out), .sel(comparator_1_gt));
  or or_1 (or_1_out, comparator_1_gt, comparator_2_lt);
  Multiplexer #(.width(18), .enable("false")) multiplexer_2 (
    .in0(adder_1_out), .in1(multiplexer_1_out), .out(Out_21b[17:0]), .sel(or_1_out));
  // Probe on {3'b000, Out_21b[17:0]}

  assign Out_21b[20:18] = 3'b000;
endmodule

module Multiply_18b (
  input  [17:0] A,
  input  [7:0] B,
  output [17:0] Product
);

  wire [17:0] adder_1_out, adder_2_out, adder_3_out, adder_4_out, adder_5_out, adder_6_out,
       multiplexer_1_out, multiplexer_2_out, multiplexer_3_out, multiplexer_4_out, multiplexer_5_out,
       multiplexer_6_out, multiplexer_7_out, multiplexer_8_out;

  Multiplexer #(.width(18), .enable("false")) multiplexer_1 (
    .in0({18{1'b0}}), .in1({A[10:0], {7{1'b0}}}), .out(multiplexer_1_out), .sel(B[7]));
  Multiplexer #(.width(18), .enable("false")) multiplexer_2 (
    .in0({18{1'b0}}), .in1({A[11:0], {6{1'b0}}}), .out(multiplexer_2_out), .sel(B[6]));
  Multiplexer #(.width(18), .enable("false")) multiplexer_3 (
    .in0({18{1'b0}}), .in1({A[12:0], {5{1'b0}}}), .out(multiplexer_3_out), .sel(B[5]));
  Adder #(.width(18)) adder_1 (.a(multiplexer_1_out), .b(multiplexer_2_out), .out(adder_1_out));  // open: cin, cout
  Adder #(.width(18)) adder_2 (.a(adder_1_out), .b(multiplexer_3_out), .out(adder_2_out));  // open: cin, cout
  Multiplexer #(.width(18), .enable("false")) multiplexer_4 (
    .in0({18{1'b0}}), .in1({A[13:0], 4'b0000}), .out(multiplexer_4_out), .sel(B[4]));
  Multiplexer #(.width(18), .enable("false")) multiplexer_5 (
    .in0({18{1'b0}}), .in1({A[14:0], 3'b000}), .out(multiplexer_5_out), .sel(B[3]));
  Adder #(.width(18)) adder_3 (.a(adder_2_out), .b(multiplexer_4_out), .out(adder_3_out));  // open: cin, cout
  Multiplexer #(.width(18), .enable("false")) multiplexer_6 (
    .in0({18{1'b0}}), .in1({A[15:0], 2'b00}), .out(multiplexer_6_out), .sel(B[2]));
  Multiplexer #(.width(18), .enable("false")) multiplexer_7 (
    .in0({18{1'b0}}), .in1({A[16:0], 1'b0}), .out(multiplexer_7_out), .sel(B[1]));
  Adder #(.width(18)) adder_4 (.a(adder_3_out), .b(multiplexer_5_out), .out(adder_4_out));  // open: cin, cout
  Multiplexer #(.width(18), .enable("false")) multiplexer_8 (
    .in0({18{1'b0}}), .in1(A), .out(multiplexer_8_out), .sel(B[0]));
  Adder #(.width(18)) adder_5 (.a(adder_4_out), .b(multiplexer_6_out), .out(adder_5_out));  // open: cin, cout
  Adder #(.width(18)) adder_6 (.a(adder_5_out), .b(multiplexer_7_out), .out(adder_6_out));  // open: cin, cout
  Adder #(.width(18)) adder_7 (.a(adder_6_out), .b(multiplexer_8_out), .out(Product));  // open: cin, cout
endmodule
