// Logisim project Shifters.circ as structural Verilog: 1 circuit, main circuit Shift
module Shift (
  input  [7:0] Data,
  input  [2:0] Shift,
  input  Right,
  output [7:0] Result,
  output C
);

  wire multiplexer_4_out, or_1_out;
  wire [7:0] multiplexer_1_out, multiplexer_2_out;

  Multiplexer #(.select(3), .width(8), .enable("false")) multiplexer_1 (
    .in0(Data), .in1({Data[6:0], 1'b0}), .in2({Data[5:0], 2'b00}), .in3({Data[4:0], 3'b000}),
    .in4({Data[3:0], 4'b0000}), .in5({Data[2:0], {5{1'b0}}}), .in6({Data[1:0], {6{1'b0}}}),
    .in7({Data[0], {7{1'b0}}}), .out(multiplexer_1_out), .sel(Shift));
  Multiplexer #(.select(3), .width(8), .enable("false")) multiplexer_2 (
    .in0(Data), .in1({1'b0, Data[7:1]}), .in2({2'b00, Data[7:2]}), .in3({3'b000, Data[7:3]}),
    .in4({4'b0000, Data[7:4]}), .in5({{5{1'b0}}, Data[7:5]}), .in6({{6{1'b0}}, Data[7:6]}),
    .in7({{7{1'b0}}, Data[7]}), .out(multiplexer_2_out), .sel(Shift));
  Multiplexer #(.width(8), .enable("false")) multiplexer_3 (
    .in0(multiplexer_1_out), .in1(multiplexer_2_out), .out(Result), .sel(Right));
  Multiplexer #(.enable("false")) multiplexer_4 (.in0(Data[7]), .in1(Data[0]), .out(multiplexer_4_out), .sel(Right));
  or or_1 (or_1_out, Shift[2], Shift[1], Shift[0]);
  and and_1 (C, multiplexer_4_out, or_1_out);

  // Other names for the same wires on the sheet: data_in[7:0] = Data
endmodule
