// Logisim project Timer.circ as structural Verilog: 2 circuits, main circuit Timer
module Timer (
  input  [24:0] Unit,
  input  [7:0] Sleep_Time,
  input  EN,
  input  CLK,
  input  Reset,
  output [7:0] TimeOut
);

  wire count, or_1_out;
  wire [24:0] adder_1_out, Multiply_25bits_1_product, register_2_q, val;

  Multiply_25bits Multiply_25bits_1 (.A(Unit), .B(Sleep_Time), .Product(Multiply_25bits_1_product));
  Adder #(.width(25)) adder_1 (.a(register_2_q), .b(25'h1), .out(adder_1_out));  // open: cin, cout
  Register #(.width(25)) register_1 (.D(Multiply_25bits_1_product), .en(EN), .clk(CLK), .Q(val), .clr(Reset));
  Register #(.width(25)) register_2 (.D(adder_1_out), .en(count), .clk(CLK), .Q(register_2_q), .clr(or_1_out));
  or or_1 (or_1_out, Reset, EN);
  // Probe on val
  Comparator #(.width(25), .mode("unsigned")) comparator_1 (.a(register_2_q), .b(val), .lt(count));  // open: gt, eq
  not not_1 (TimeOut[0], count);

  assign TimeOut[7:1] = {7{1'b0}};

  // Other names for the same wires on the sheet: ld = EN; R = Reset
endmodule

module Multiply_25bits (
  input  [24:0] A,
  input  [7:0] B,
  output [24:0] Product
);

  wire [24:0] adder_1_out, adder_2_out, adder_3_out, adder_4_out, adder_5_out, adder_6_out,
       multiplexer_1_out, multiplexer_2_out, multiplexer_3_out, multiplexer_4_out, multiplexer_5_out,
       multiplexer_6_out, multiplexer_7_out, multiplexer_8_out;

  Multiplexer #(.width(25), .enable("false")) multiplexer_1 (
    .in0({25{1'b0}}), .in1({A[17:0], {7{1'b0}}}), .out(multiplexer_1_out), .sel(B[7]));
  Multiplexer #(.width(25), .enable("false")) multiplexer_2 (
    .in0({25{1'b0}}), .in1({A[18:0], {6{1'b0}}}), .out(multiplexer_2_out), .sel(B[6]));
  Multiplexer #(.width(25), .enable("false")) multiplexer_3 (
    .in0({25{1'b0}}), .in1({A[19:0], {5{1'b0}}}), .out(multiplexer_3_out), .sel(B[5]));
  Adder #(.width(25)) adder_1 (.a(multiplexer_1_out), .b(multiplexer_2_out), .out(adder_1_out));  // open: cin, cout
  Adder #(.width(25)) adder_2 (.a(adder_1_out), .b(multiplexer_3_out), .out(adder_2_out));  // open: cin, cout
  Multiplexer #(.width(25), .enable("false")) multiplexer_4 (
    .in0({25{1'b0}}), .in1({A[20:0], 4'b0000}), .out(multiplexer_4_out), .sel(B[4]));
  Multiplexer #(.width(25), .enable("false")) multiplexer_5 (
    .in0({25{1'b0}}), .in1({A[21:0], 3'b000}), .out(multiplexer_5_out), .sel(B[3]));
  Adder #(.width(25)) adder_3 (.a(adder_2_out), .b(multiplexer_4_out), .out(adder_3_out));  // open: cin, cout
  Multiplexer #(.width(25), .enable("false")) multiplexer_6 (
    .in0({25{1'b0}}), .in1({A[22:0], 2'b00}), .out(multiplexer_6_out), .sel(B[2]));
  Multiplexer #(.width(25), .enable("false")) multiplexer_7 (
    .in0({25{1'b0}}), .in1({A[23:0], 1'b0}), .out(multiplexer_7_out), .sel(B[1]));
  Adder #(.width(25)) adder_4 (.a(adder_3_out), .b(multiplexer_5_out), .out(adder_4_out));  // open: cin, cout
  Multiplexer #(.width(25), .enable("false")) multiplexer_8 (
    .in0({25{1'b0}}), .in1(A), .out(multiplexer_8_out), .sel(B[0]));
  Adder #(.width(25)) adder_5 (.a(adder_4_out), .b(multiplexer_6_out), .out(adder_5_out));  // open: cin, cout
  Adder #(.width(25)) adder_6 (.a(adder_5_out), .b(multiplexer_7_out), .out(adder_6_out));  // open: cin, cout
  Adder #(.width(25)) adder_7 (.a(adder_6_out), .b(multiplexer_8_out), .out(Product));  // open: cin, cout
endmodule
