// Logisim project UART_8bit.circ as structural Verilog: 4 circuits, main circuit Send
module Network_Card (
  input  [7:0] Data_In,
  input  EN,
  input  UART_INPUT,
  input  clk,
  input  Reset,
  output UART_OUTPUT,
  output [7:0] Data_Out,
  output [7:0] Online
);

  wire and_2_out, counter_1_carry, or_1_out, or_2_out, Parity_2_outp, Rec, Receive_1_received, xnor_1_out;
  wire [0:0] Parity_1_outp;
  wire [7:0] Receive_1_value;

  Parity Parity_1 (.Data(Data_In[7:1]), .Outp(Parity_1_outp[0]));
  or or_1 (or_1_out, Rec, Reset);
  Counter #(.width(26), .max('h2faf080), .ongoal("stay")) counter_1 (
    .clr(or_1_out), .clk(clk), .carry(counter_1_carry));  // open: load, up, count, D, Q
  Receive Receive_1 (
    .UART_INPUT(UART_INPUT), .clk(clk), .Reset(Reset), .Value(Receive_1_value), .Received(Receive_1_received));
  Send Send_1 (
    .Data_In({Data_In[7:1], Parity_1_outp[0]}), .LD(EN), .CLK(clk), .Reset(Reset), .UART_OUTPUT(UART_OUTPUT));
  Parity Parity_2 (.Data(Receive_1_value[7:1]), .Outp(Parity_2_outp));
  and and_1 (Rec, Receive_1_received, xnor_1_out);
  and and_2 (and_2_out, ~counter_1_carry, Online[0]);  // AND_Gate
  xnor xnor_1 (xnor_1_out, Parity_2_outp, Receive_1_value[0]);
  D_Flip_Flop d_ff_1 (.D(or_2_out), .clk(clk), .Q(Online[0]), .reset(Reset));  // open: Qn, preset
  or or_2 (or_2_out, Rec, and_2_out);
  Register register_1 (.D(Receive_1_value), .en(Rec), .clk(clk), .Q(Data_Out));  // open: clr

  assign Online[7:1] = {7{1'b0}};

  // Other names for the same wires on the sheet: LD = EN; R = Reset; U_INP = UART_INPUT
endmodule

module Send (
  input  [7:0] Data_In,
  input  LD,
  input  CLK,
  input  Reset,
  output UART_OUTPUT
);

  wire and_2_out, b, end_s, ld_t, Nb_Shifts_carry, or_1_out, or_2_out, or_3_out, or_4_out, shift,
       shift_register_1_p15;

  or or_1 (or_1_out, Reset, ld_t);
  Counter #(.width(14), .max('h28b0)) Time_Base (
    .clr(or_1_out), .clk(CLK), .carry(shift));  // open: load, up, count, D, Q
  and and_1 (ld_t, ~b, LD);  // AND_Gate
  // Probe on ld_t
  // Shift_Register #(.length(9)) shift_register_1: pin names not known; wires that end beside it: Reset, ld_t, shift, CLK, 1'b1, Data_In[0], Data_In[1], Data_In[2], Data_In[3], Data_In[4], Data_In[5], Data_In[6], Data_In[7], 1'b0, shift_register_1_p15
  // Probe on shift
  Counter #(.width(4), .max('h9)) Nb_Shifts (
    .clr(or_2_out), .count(shift), .clk(CLK), .carry(Nb_Shifts_carry));  // open: load, up, D, Q
  or or_2 (or_2_out, Reset, ld_t);
  and and_2 (and_2_out, b, ~end_s);  // AND_Gate
  or or_3 (or_3_out, ld_t, and_2_out);
  D_Flip_Flop Busy (.D(or_3_out), .clk(CLK), .Q(b), .reset(or_4_out));  // open: Qn, preset
  or or_4 (or_4_out, end_s, Reset);
  Multiplexer #(.enable("false")) multiplexer_1 (.in0(1'b1), .in1(shift_register_1_p15), .out(UART_OUTPUT), .sel(b));
  and and_3 (end_s, shift, Nb_Shifts_carry);

  // Other names for the same wires on the sheet: data[7:0] = Data_In; R = Reset
endmodule

module Receive (
  input  UART_INPUT,
  input  clk,
  input  Reset,
  output [7:0] Value,
  output Received
);

  wire and_1_out, and_4_out, and_6_out, dephased, end_rec, half, incomming, inp, Nb_Shifts_carry, not_1_out,
       or_1_out, or_2_out, or_4_out, or_5_out, rec, shift, Shift_p1, start, stp_bit;
  wire [13:0] Time_Base_q;

  not not_1 (not_1_out, UART_INPUT);
  and and_1 (and_1_out, start, ~rec);  // AND_Gate
  nor nor_1 (incomming, rec, inp, start);
  D_Flip_Flop Input (.D(not_1_out), .clk(clk), .Qn(inp), .reset(Reset));  // open: Q, preset
  D_Flip_Flop u_start (.D(or_1_out), .clk(clk), .Q(start), .reset(Reset));  // open: Qn, preset
  or or_1 (or_1_out, and_1_out, incomming);
  Counter #(.width(14), .max('h28b0)) Time_Base (
    .clr(Reset), .load(or_2_out), .clk(clk), .D(14'h1), .carry(shift), .Q(Time_Base_q));  // open: up, count
  or or_2 (or_2_out, incomming, dephased);
  // Probe on inp
  // Shift_Register #(.length(9)) Shift: pin names not known; wires that end beside it: Shift_p1, shift, clk, inp, stp_bit, Value[0], Value[1], Value[2], Value[3], Value[4], Value[5], Value[6], Value[7]
  or or_3 (Shift_p1, start, Reset);
  // Probe on shift
  and and_2 (half, ~Time_Base_q[0], ~Time_Base_q[1], ~Time_Base_q[2], Time_Base_q[3], Time_Base_q[4], ~Time_Base_q[5], Time_Base_q[6], ~Time_Base_q[7], ~Time_Base_q[8], ~Time_Base_q[9], Time_Base_q[10], ~Time_Base_q[11], Time_Base_q[12], ~Time_Base_q[13]);  // AND_Gate
  // Probe on Value
  and and_3 (dephased, start, half);
  and and_4 (and_4_out, rec, ~end_rec);  // AND_Gate
  or or_4 (or_4_out, Reset, incomming);
  and and_5 (Received, ~or_5_out, rec, stp_bit);  // AND_Gate
  D_Flip_Flop Receiving (.D(or_5_out), .clk(clk), .Q(rec), .reset(Reset));  // open: Qn, preset
  or or_5 (or_5_out, dephased, and_4_out);
  Counter #(.width(4), .max('h8)) Nb_Shifts (
    .clr(or_4_out), .count(shift), .clk(clk), .carry(Nb_Shifts_carry));  // open: load, up, D, Q
  D_Flip_Flop d_ff_1 (.D(and_6_out), .clk(clk), .Q(end_rec), .reset(Reset));  // open: Qn, preset
  and and_6 (and_6_out, shift, Nb_Shifts_carry);

  // Other names for the same wires on the sheet: R = Reset

  // Notes on the sheet:
  //   Evite le chargement accidentel au démarrage
endmodule

module Parity (
  input  [6:0] Data,
  output Outp
);

  wire xor_1_out, xor_2_out, xor_3_out, xor_4_out, xor_5_out;

  xor xor_1 (xor_1_out, Data[0], Data[1]);
  xor xor_2 (xor_2_out, xor_1_out, Data[2]);
  xor xor_3 (xor_3_out, xor_2_out, Data[3]);
  xor xor_4 (xor_4_out, xor_3_out, Data[4]);
  xor xor_5 (xor_5_out, xor_4_out, Data[5]);
  xnor xnor_1 (Outp, xor_5_out, Data[6]);
endmodule
