// Logisim project 7_seg4.circ as structural Verilog: 1 circuit, main circuit Hex_7_seg_seq
module Hex_7_seg_seq (
  input  Clk,
  input  [3:0] Hex_7_Seg_0,
  input  [3:0] Hex_7_Seg_1,
  input  [3:0] Hex_7_Seg_2,
  input  [3:0] Hex_7_Seg_3,
  output [3:0] Seg_Selector,
  output a,
  output b,
  output c,
  output d,
  output e,
  output f,
  output g
);

  wire Cpt_carry, not_1_out, not_2_out;
  wire [1:0] Cpt_2_q;
  wire [3:0] multiplexer_1_out;

  not not_1 (not_1_out, 1'b1);
  Counter #(.width(17), .max('h1869f), .ongoal("continue")) Cpt (
    .load(not_1_out), .up(1'b1), .clk(Clk), .carry(Cpt_carry));  // open: clr, count, D, Q
  Counter #(.width(2), .max('h3), .ongoal("continue")) Cpt_2 (
    .load(not_2_out), .up(1'b1), .count(Cpt_carry), .clk(Clk), .Q(Cpt_2_q));  // open: clr, D, carry
  not not_2 (not_2_out, 1'b1);
  Decoder #(.select(2), .enable("false")) decoder_1 (
    .out0(Seg_Selector[0]), .out1(Seg_Selector[1]), .out2(Seg_Selector[2]), .out3(Seg_Selector[3]),
    .sel(Cpt_2_q));
  Multiplexer #(.select(2), .width(4), .enable("false")) multiplexer_1 (
    .in0(Hex_7_Seg_0), .in1(Hex_7_Seg_1), .in2(Hex_7_Seg_2), .in3(Hex_7_Seg_3), .out(multiplexer_1_out),
    .sel(Cpt_2_q));
  Hex_7Seg Seg (.Seg_Input(multiplexer_1_out), .Output_1({g, f, e, d, c, b, a}));
endmodule
