// Logisim project 7seg.circ as structural Verilog: 8 circuits, main circuit Hex_7Seg
module Hex_7Seg (
  input  [3:0] Seg_Input,
  output [6:0] Output_1
);

  A A_1 (.a(Seg_Input[3]), .b(Seg_Input[2]), .c(Seg_Input[1]), .d(Seg_Input[0]), .A_Out(Output_1[0]));
  B B_1 (.a(Seg_Input[3]), .b(Seg_Input[2]), .c(Seg_Input[1]), .d(Seg_Input[0]), .B_out(Output_1[1]));
  C C_1 (.a(Seg_Input[3]), .b(Seg_Input[2]), .c(Seg_Input[1]), .d(Seg_Input[0]), .C_out(Output_1[2]));
  D D_1 (.a(Seg_Input[3]), .b(Seg_Input[2]), .c(Seg_Input[1]), .d(Seg_Input[0]), .D_out(Output_1[3]));
  E E_1 (.a(Seg_Input[3]), .b(Seg_Input[2]), .c(Seg_Input[1]), .d(Seg_Input[0]), .E_out(Output_1[4]));
  F F_1 (.a(Seg_Input[3]), .b(Seg_Input[2]), .c(Seg_Input[1]), .d(Seg_Input[0]), .F_out(Output_1[5]));
  G G_1 (.a(Seg_Input[3]), .b(Seg_Input[2]), .c(Seg_Input[1]), .d(Seg_Input[0]), .G_out(Output_1[6]));
endmodule

module A (
  input  a,
  input  b,
  input  c,
  input  d,
  output A_Out
);

  wire and_1_out, and_2_out, and_3_out, and_4_out, and_5_out, and_6_out, nand_1_out, or_1_out;

  and and_1 (and_1_out, ~a, d);  // AND_Gate
  or or_1 (or_1_out, and_1_out, c);
  and and_2 (and_2_out, b, or_1_out);
  and and_3 (and_3_out, ~a, c);  // AND_Gate
  and and_4 (and_4_out, a, ~c);  // AND_Gate
  nand nand_1 (nand_1_out, b, d);
  and and_5 (and_5_out, and_4_out, nand_1_out);
  and and_6 (and_6_out, ~b, ~d);  // AND_Gate
  or or_2 (A_Out, and_2_out, and_5_out, and_6_out, and_3_out);
endmodule

module B (
  input  a,
  input  b,
  input  c,
  input  d,
  output B_out
);

  wire and_1_out, nand_1_out, nor_1_out, nor_2_out, xor_1_out, xor_2_out;

  xor xor_1 (xor_1_out, a, d);
  nand nand_1 (nand_1_out, a, d);
  nor nor_1 (nor_1_out, c, xor_1_out);
  and and_1 (and_1_out, nand_1_out, ~b);  // AND_Gate
  xor xor_2 (xor_2_out, c, d);
  nor nor_2 (nor_2_out, a, xor_2_out);
  or or_1 (B_out, and_1_out, nor_2_out, nor_1_out);
endmodule

module C (
  input  a,
  input  b,
  input  c,
  input  d,
  output C_out
);

  wire and_1_out, and_2_out, or_1_out, xor_1_out;

  xor xor_1 (xor_1_out, a, b);
  and and_1 (and_1_out, ~c, d);  // AND_Gate
  or or_1 (or_1_out, ~c, d);  // OR_Gate
  and and_2 (and_2_out, ~a, or_1_out);  // AND_Gate
  or or_2 (C_out, xor_1_out, and_2_out, and_1_out);
endmodule

module D (
  input  a,
  input  b,
  input  c,
  input  d,
  output D_out
);

  wire and_1_out, and_2_out, and_3_out, and_4_out, and_5_out, or_1_out, xor_1_out;

  and and_1 (and_1_out, ~a, ~d);  // AND_Gate
  and and_2 (and_2_out, c, d);
  xor xor_1 (xor_1_out, c, d);
  and and_3 (and_3_out, a, ~c);  // AND_Gate
  or or_1 (or_1_out, and_1_out, and_2_out);
  and and_4 (and_4_out, ~b, or_1_out);  // AND_Gate
  and and_5 (and_5_out, b, xor_1_out);
  or or_2 (D_out, and_4_out, and_5_out, and_3_out);
endmodule

module E (
  input  a,
  input  b,
  input  c,
  input  d,
  output E_out
);

  wire and_1_out, and_2_out, and_3_out, and_4_out, or_1_out, or_2_out;

  and and_1 (and_1_out, a, b);
  and and_2 (and_2_out, ~b, ~d);  // AND_Gate
  or or_1 (or_1_out, a, ~d);  // OR_Gate
  or or_2 (or_2_out, and_1_out, and_2_out);
  and and_3 (and_3_out, c, or_1_out);
  and and_4 (and_4_out, or_2_out, ~c);  // AND_Gate
  or or_3 (E_out, and_4_out, and_3_out);
endmodule

module F (
  input  a,
  input  b,
  input  c,
  input  d,
  output F_out
);

  wire and_1_out, and_2_out, and_3_out, and_4_out, and_5_out, or_1_out, or_2_out;

  and and_1 (and_1_out, ~a, ~c);  // AND_Gate
  and and_2 (and_2_out, ~c, ~d);  // AND_Gate
  or or_1 (or_1_out, and_2_out, a);
  or or_2 (or_2_out, and_1_out, ~d);  // OR_Gate
  and and_3 (and_3_out, b, or_2_out);
  and and_4 (and_4_out, ~b, or_1_out);  // AND_Gate
  and and_5 (and_5_out, a, c, d);
  or or_3 (F_out, and_3_out, and_4_out, and_5_out);
endmodule

module G (
  input  a,
  input  b,
  input  c,
  input  d,
  output G_out
);

  wire and_1_out, and_2_out, and_3_out, or_1_out, xor_1_out;

  xor xor_1 (xor_1_out, b, c);
  and and_1 (and_1_out, ~a, xor_1_out);  // AND_Gate
  or or_1 (or_1_out, ~b, d);  // OR_Gate
  and and_2 (and_2_out, c, ~d);  // AND_Gate
  and and_3 (and_3_out, or_1_out, a);
  or or_2 (G_out, and_1_out, and_3_out, and_2_out);
endmodule
