// Logisim project test_7seg.circ as structural Verilog: 1 circuit, main circuit main
module main (
  input  clk,
  input  [15:0] inp,
  output [3:0] Seg_Select,
  output a,
  output b,
  output c,
  output d,
  output e,
  output f,
  output g
);

  Hex_7_seg_seq Hex_7_seg_seq_1 (
    .Clk(clk), .Hex_7_Seg_0(inp[3:0]), .Hex_7_Seg_1(inp[7:4]), .Hex_7_Seg_2(inp[11:8]),
    .Hex_7_Seg_3(inp[15:12]), .Seg_Selector(Seg_Select), .a(a), .b(b), .c(c), .d(d), .e(e), .f(f), .g(g));
endmodule
