// Logisim project envoi.circ as structural Verilog: 1 circuit, main circuit ROM_CPU
module ROM_CPU (
  input  [6:0] Addr,
  output [15:0] Instr
);

  wire [15:0] mux0, mux1, mux2, mux3, undriven, undriven_2, undriven_3, undriven_4, undriven_5, undriven_6,
       undriven_7, undriven_8, undriven_9, undriven_10, undriven_11, undriven_12, undriven_13, undriven_14,
       undriven_15, undriven_16, undriven_17, undriven_18, undriven_19, undriven_20, undriven_21,
       undriven_22, undriven_23, undriven_24, undriven_25, undriven_26, undriven_27, undriven_28,
       undriven_29, undriven_30, undriven_31, undriven_32, undriven_33, undriven_34, undriven_35,
       undriven_36, undriven_37, undriven_38, undriven_39, undriven_40, undriven_41, undriven_42,
       undriven_43, undriven_44, undriven_45, undriven_46, undriven_47, undriven_48, undriven_49,
       undriven_50, undriven_51, undriven_52, undriven_53, undriven_54, undriven_55, undriven_56,
       undriven_57, undriven_58, undriven_59, undriven_60, undriven_61, undriven_62, undriven_63,
       undriven_64, undriven_65, undriven_66, undriven_67, undriven_68, undriven_69, undriven_70,
       undriven_71, undriven_72, undriven_73, undriven_74, undriven_75, undriven_76, undriven_77,
       undriven_78, undriven_79;

  Multiplexer #(.select(5), .width(16), .enable("false")) multiplexer_1 (
    .in0(16'hc004), .in1(16'h3218), .in2(16'h8440), .in3(16'h250), .in4(16'h9240), .in5(16'hd201),
    .in6(16'h8205), .in7(16'hd200), .in8(16'h8401), .in9(16'hc200), .in10(16'h1650), .in11(16'ha4fe),
    .in12(16'h2220), .in13(16'h3258), .in14(16'h8460), .in15(16'h250), .in16(16'h9240), .in17(16'hd201),
    .in18(16'h8205), .in19(16'hd200), .in20(16'h8401), .in21(16'hc200), .in22(16'h1650), .in23(16'ha4fe),
    .in24(16'hc005), .in25(16'h3218), .in26(16'h8480), .in27(16'h250), .in28(16'h9240), .in29(16'hd201),
    .in30(16'h8205), .in31(16'hd200), .out(mux0), .sel(Addr[4:0]));
  Multiplexer #(.select(5), .width(16), .enable("false")) multiplexer_2 (
    .in0(16'h8401), .in1(16'hc200), .in2(16'h1650), .in3(16'ha4fe), .in4(16'h2220), .in5(16'h3258),
    .in6(16'h84a0), .in7(16'h250), .in8(16'h9240), .in9(16'hd201), .in10(16'h8205), .in11(16'hd200),
    .in12(16'h8401), .in13(16'hc200), .in14(16'h1650), .in15(16'ha4fe), .in16(16'hb000), .in17(undriven_8),
    .in18(undriven), .in19(undriven_9), .in20(undriven_2), .in21(undriven_10), .in22(undriven_3),
    .in23(undriven_11), .in24(undriven_4), .in25(undriven_12), .in26(undriven_5), .in27(undriven_13),
    .in28(undriven_6), .in29(undriven_14), .in30(undriven_7), .in31(undriven_15), .out(mux1), .sel(Addr[4:0]));
  Multiplexer #(.select(5), .width(16), .enable("false")) multiplexer_3 (
    .in0(undriven_16), .in1(undriven_48), .in2(undriven_17), .in3(undriven_49), .in4(undriven_18),
    .in5(undriven_50), .in6(undriven_19), .in7(undriven_51), .in8(undriven_20), .in9(undriven_52),
    .in10(undriven_21), .in11(undriven_53), .in12(undriven_22), .in13(undriven_54), .in14(undriven_23),
    .in15(undriven_55), .in16(undriven_24), .in17(undriven_56), .in18(undriven_25), .in19(undriven_57),
    .in20(undriven_26), .in21(undriven_58), .in22(undriven_27), .in23(undriven_59), .in24(undriven_28),
    .in25(undriven_60), .in26(undriven_29), .in27(undriven_61), .in28(undriven_30), .in29(undriven_62),
    .in30(undriven_31), .in31(undriven_63), .out(mux2), .sel(Addr[4:0]));
  Multiplexer #(.select(5), .width(16), .enable("false")) multiplexer_4 (
    .in0(undriven_32), .in1(undriven_64), .in2(undriven_33), .in3(undriven_65), .in4(undriven_34),
    .in5(undriven_66), .in6(undriven_35), .in7(undriven_67), .in8(undriven_36), .in9(undriven_68),
    .in10(undriven_37), .in11(undriven_69), .in12(undriven_38), .in13(undriven_70), .in14(undriven_39),
    .in15(undriven_71), .in16(undriven_40), .in17(undriven_72), .in18(undriven_41), .in19(undriven_73),
    .in20(undriven_42), .in21(undriven_74), .in22(undriven_43), .in23(undriven_75), .in24(undriven_44),
    .in25(undriven_76), .in26(undriven_45), .in27(undriven_77), .in28(undriven_46), .in29(undriven_78),
    .in30(undriven_47), .in31(undriven_79), .out(mux3), .sel(Addr[4:0]));
  Multiplexer #(.select(2), .width(16), .enable("false")) multiplexer_5 (
    .in0(mux0), .in1(mux1), .in2(mux2), .in3(mux3), .out(Instr), .sel(Addr[6:5]));
  // Probe on Instr

  // Other names for the same wires on the sheet: sel[1:0] = Addr[6:5]
endmodule
