// Logisim project fibo.circ as structural Verilog: 1 circuit, main circuit ROM_CPU
module ROM_CPU (
  input  [6:0] Addr,
  output [15:0] Instr
);

  wire [15:0] mux0, mux1, mux2, mux3, undriven, undriven_2, undriven_3, undriven_4, undriven_5, undriven_6,
       undriven_7, undriven_8, undriven_9, undriven_10, undriven_11, undriven_12, undriven_13, undriven_14,
       undriven_15, undriven_16, undriven_17, undriven_18, undriven_19, undriven_20, undriven_21,
       undriven_22, undriven_23, undriven_24, undriven_25, undriven_26, undriven_27, undriven_28,
       undriven_29, undriven_30, undriven_31, undriven_32, undriven_33, undriven_34, undriven_35,
       undriven_36, undriven_37, undriven_38, undriven_39, undriven_40, undriven_41, undriven_42,
       undriven_43, undriven_44, undriven_45, undriven_46, undriven_47, undriven_48, undriven_49,
       undriven_50, undriven_51, undriven_52, undriven_53, undriven_54, undriven_55, undriven_56,
       undriven_57, undriven_58, undriven_59, undriven_60, undriven_61, undriven_62, undriven_63,
       undriven_64, undriven_65, undriven_66, undriven_67, undriven_68, undriven_69, undriven_70,
       undriven_71, undriven_72, undriven_73, undriven_74, undriven_75, undriven_76, undriven_77,
       undriven_78, undriven_79, undriven_80, undriven_81, undriven_82, undriven_83, undriven_84,
       undriven_85, undriven_86, undriven_87, undriven_88, undriven_89, undriven_90, undriven_91,
       undriven_92, undriven_93, undriven_94, undriven_95, undriven_96, undriven_97, undriven_98,
       undriven_99, undriven_100, undriven_101, undriven_102, undriven_103, undriven_104, undriven_105,
       undriven_106, undriven_107, undriven_108, undriven_109, undriven_110, undriven_111, undriven_112,
       undriven_113, undriven_114, undriven_115, undriven_116, undriven_117, undriven_118, undriven_119,
       undriven_120;

  Multiplexer #(.select(5), .width(16), .enable("false")) multiplexer_1 (
    .in0(16'h8000), .in1(16'h8200), .in2(16'h8401), .in3(16'h640), .in4(16'h280), .in5(16'h498),
    .in6(16'ha400), .in7(16'hbffc), .in8(undriven), .in9(undriven_29), .in10(undriven_2), .in11(undriven_30),
    .in12(undriven_3), .in13(undriven_31), .in14(undriven_4), .in15(undriven_32), .in16(undriven_5),
    .in17(undriven_33), .in18(undriven_6), .in19(undriven_34), .in20(undriven_7), .in21(undriven_35),
    .in22(undriven_8), .in23(undriven_36), .in24(undriven_9), .in25(undriven_37), .in26(undriven_10),
    .in27(undriven_38), .in28(undriven_11), .in29(undriven_39), .in30(undriven_12), .in31(undriven_40),
    .out(mux0), .sel(Addr[4:0]));
  Multiplexer #(.select(5), .width(16), .enable("false")) multiplexer_2 (
    .in0(undriven_13), .in1(undriven_41), .in2(undriven_14), .in3(undriven_42), .in4(undriven_15),
    .in5(undriven_43), .in6(undriven_16), .in7(undriven_44), .in8(undriven_17), .in9(undriven_45),
    .in10(undriven_18), .in11(undriven_46), .in12(undriven_19), .in13(undriven_47), .in14(undriven_20),
    .in15(undriven_48), .in16(undriven_21), .in17(undriven_49), .in18(undriven_22), .in19(undriven_50),
    .in20(undriven_23), .in21(undriven_51), .in22(undriven_24), .in23(undriven_52), .in24(undriven_25),
    .in25(undriven_53), .in26(undriven_26), .in27(undriven_54), .in28(undriven_27), .in29(undriven_55),
    .in30(undriven_28), .in31(undriven_56), .out(mux1), .sel(Addr[4:0]));
  Multiplexer #(.select(5), .width(16), .enable("false")) multiplexer_3 (
    .in0(undriven_57), .in1(undriven_89), .in2(undriven_58), .in3(undriven_90), .in4(undriven_59),
    .in5(undriven_91), .in6(undriven_60), .in7(undriven_92), .in8(undriven_61), .in9(undriven_93),
    .in10(undriven_62), .in11(undriven_94), .in12(undriven_63), .in13(undriven_95), .in14(undriven_64),
    .in15(undriven_96), .in16(undriven_65), .in17(undriven_97), .in18(undriven_66), .in19(undriven_98),
    .in20(undriven_67), .in21(undriven_99), .in22(undriven_68), .in23(undriven_100), .in24(undriven_69),
    .in25(undriven_101), .in26(undriven_70), .in27(undriven_102), .in28(undriven_71), .in29(undriven_103),
    .in30(undriven_72), .in31(undriven_104), .out(mux2), .sel(Addr[4:0]));
  Multiplexer #(.select(5), .width(16), .enable("false")) multiplexer_4 (
    .in0(undriven_73), .in1(undriven_105), .in2(undriven_74), .in3(undriven_106), .in4(undriven_75),
    .in5(undriven_107), .in6(undriven_76), .in7(undriven_108), .in8(undriven_77), .in9(undriven_109),
    .in10(undriven_78), .in11(undriven_110), .in12(undriven_79), .in13(undriven_111), .in14(undriven_80),
    .in15(undriven_112), .in16(undriven_81), .in17(undriven_113), .in18(undriven_82), .in19(undriven_114),
    .in20(undriven_83), .in21(undriven_115), .in22(undriven_84), .in23(undriven_116), .in24(undriven_85),
    .in25(undriven_117), .in26(undriven_86), .in27(undriven_118), .in28(undriven_87), .in29(undriven_119),
    .in30(undriven_88), .in31(undriven_120), .out(mux3), .sel(Addr[4:0]));
  Multiplexer #(.select(2), .width(16), .enable("false")) multiplexer_5 (
    .in0(mux0), .in1(mux1), .in2(mux2), .in3(mux3), .out(Instr), .sel(Addr[6:5]));
  // Probe on Instr

  // Other names for the same wires on the sheet: sel[1:0] = Addr[6:5]
endmodule
