// Logisim project test.circ as structural Verilog: 1 circuit, main circuit ROM_CPU
module ROM_CPU (
  input  [6:0] Addr,
  output [15:0] Instr
);

  wire [15:0] mux0, mux1, mux2, mux3;

  Multiplexer #(.select(5), .width(16), .enable("false")) multiplexer_1 (
    .in0(16'hc004), .in1(16'hd002), .in2(16'hb000), .in3({16{1'b0}}), .in4({16{1'b0}}), .in5({16{1'b0}}),
    .in6({16{1'b0}}), .in7({16{1'b0}}), .in8({16{1'b0}}), .in9({16{1'b0}}), .in10({16{1'b0}}),
    .in11({16{1'b0}}), .in12({16{1'b0}}), .in13({16{1'b0}}), .in14({16{1'b0}}), .in15({16{1'b0}}),
    .in16({16{1'b0}}), .in17({16{1'b0}}), .in18({16{1'b0}}), .in19({16{1'b0}}), .in20({16{1'b0}}),
    .in21({16{1'b0}}), .in22({16{1'b0}}), .in23({16{1'b0}}), .in24({16{1'b0}}), .in25({16{1'b0}}),
    .in26({16{1'b0}}), .in27({16{1'b0}}), .in28({16{1'b0}}), .in29({16{1'b0}}), .in30({16{1'b0}}),
    .in31({16{1'b0}}), .out(mux0), .sel(Addr[4:0]));
  Multiplexer #(.select(5), .width(16), .enable("false")) multiplexer_2 (
    .in0({16{1'b0}}), .in1({16{1'b0}}), .in2({16{1'b0}}), .in3({16{1'b0}}), .in4({16{1'b0}}),
    .in5({16{1'b0}}), .in6({16{1'b0}}), .in7({16{1'b0}}), .in8({16{1'b0}}), .in9({16{1'b0}}),
    .in10({16{1'b0}}), .in11({16{1'b0}}), .in12({16{1'b0}}), .in13({16{1'b0}}), .in14({16{1'b0}}),
    .in15({16{1'b0}}), .in16({16{1'b0}}), .in17({16{1'b0}}), .in18({16{1'b0}}), .in19({16{1'b0}}),
    .in20({16{1'b0}}), .in21({16{1'b0}}), .in22({16{1'b0}}), .in23({16{1'b0}}), .in24({16{1'b0}}),
    .in25({16{1'b0}}), .in26({16{1'b0}}), .in27({16{1'b0}}), .in28({16{1'b0}}), .in29({16{1'b0}}),
    .in30({16{1'b0}}), .in31({16{1'b0}}), .out(mux1), .sel(Addr[4:0]));
  Multiplexer #(.select(5), .width(16), .enable("false")) multiplexer_3 (
    .in0({16{1'b0}}), .in1({16{1'b0}}), .in2({16{1'b0}}), .in3({16{1'b0}}), .in4({16{1'b0}}),
    .in5({16{1'b0}}), .in6({16{1'b0}}), .in7({16{1'b0}}), .in8({16{1'b0}}), .in9({16{1'b0}}),
    .in10({16{1'b0}}), .in11({16{1'b0}}), .in12({16{1'b0}}), .in13({16{1'b0}}), .in14({16{1'b0}}),
    .in15({16{1'b0}}), .in16({16{1'b0}}), .in17({16{1'b0}}), .in18({16{1'b0}}), .in19({16{1'b0}}),
    .in20({16{1'b0}}), .in21({16{1'b0}}), .in22({16{1'b0}}), .in23({16{1'b0}}), .in24({16{1'b0}}),
    .in25({16{1'b0}}), .in26({16{1'b0}}), .in27({16{1'b0}}), .in28({16{1'b0}}), .in29({16{1'b0}}),
    .in30({16{1'b0}}), .in31({16{1'b0}}), .out(mux2), .sel(Addr[4:0]));
  Multiplexer #(.select(5), .width(16), .enable("false")) multiplexer_4 (
    .in0({16{1'b0}}), .in1({16{1'b0}}), .in2({16{1'b0}}), .in3({16{1'b0}}), .in4({16{1'b0}}),
    .in5({16{1'b0}}), .in6({16{1'b0}}), .in7({16{1'b0}}), .in8({16{1'b0}}), .in9({16{1'b0}}),
    .in10({16{1'b0}}), .in11({16{1'b0}}), .in12({16{1'b0}}), .in13({16{1'b0}}), .in14({16{1'b0}}),
    .in15({16{1'b0}}), .in16({16{1'b0}}), .in17({16{1'b0}}), .in18({16{1'b0}}), .in19({16{1'b0}}),
    .in20({16{1'b0}}), .in21({16{1'b0}}), .in22({16{1'b0}}), .in23({16{1'b0}}), .in24({16{1'b0}}),
    .in25({16{1'b0}}), .in26({16{1'b0}}), .in27({16{1'b0}}), .in28({16{1'b0}}), .in29({16{1'b0}}),
    .in30({16{1'b0}}), .in31({16{1'b0}}), .out(mux3), .sel(Addr[4:0]));
  Multiplexer #(.select(2), .width(16), .enable("false")) multiplexer_5 (
    .in0(mux0), .in1(mux1), .in2(mux2), .in3(mux3), .out(Instr), .sel(Addr[6:5]));
  // Probe on Instr

  // Other names for the same wires on the sheet: sel[1:0] = Addr[6:5]
endmodule
