// Logisim project rom_base.circ as structural Verilog: 1 circuit, main circuit ROM_CPU
module ROM_CPU (
  input  [6:0] Addr,
  output [15:0] Instr
);

  wire [15:0] mux0, mux1, mux2, mux3, undriven, undriven_2, undriven_3, undriven_4, undriven_5, undriven_6,
       undriven_7, undriven_8, undriven_9, undriven_10, undriven_11, undriven_12, undriven_13, undriven_14,
       undriven_15, undriven_16, undriven_17, undriven_18, undriven_19, undriven_20, undriven_21,
       undriven_22, undriven_23, undriven_24, undriven_25, undriven_26, undriven_27, undriven_28,
       undriven_29, undriven_30, undriven_31, undriven_32, undriven_33, undriven_34, undriven_35,
       undriven_36, undriven_37, undriven_38, undriven_39, undriven_40, undriven_41, undriven_42,
       undriven_43, undriven_44, undriven_45, undriven_46, undriven_47, undriven_48, undriven_49,
       undriven_50, undriven_51, undriven_52, undriven_53, undriven_54, undriven_55, undriven_56,
       undriven_57, undriven_58, undriven_59, undriven_60, undriven_61, undriven_62, undriven_63,
       undriven_64, undriven_65, undriven_66, undriven_67, undriven_68, undriven_69, undriven_70,
       undriven_71, undriven_72, undriven_73, undriven_74, undriven_75, undriven_76, undriven_77,
       undriven_78, undriven_79, undriven_80, undriven_81, undriven_82, undriven_83, undriven_84,
       undriven_85, undriven_86, undriven_87, undriven_88, undriven_89, undriven_90, undriven_91,
       undriven_92, undriven_93, undriven_94, undriven_95, undriven_96, undriven_97, undriven_98,
       undriven_99, undriven_100, undriven_101, undriven_102, undriven_103, undriven_104, undriven_105,
       undriven_106, undriven_107, undriven_108, undriven_109, undriven_110, undriven_111, undriven_112,
       undriven_113, undriven_114, undriven_115, undriven_116, undriven_117, undriven_118, undriven_119,
       undriven_120, undriven_121, undriven_122, undriven_123, undriven_124, undriven_125, undriven_126,
       undriven_127, undriven_128;

  Multiplexer #(.select(5), .width(16), .enable("false")) multiplexer_1 (
    .in0(undriven), .in1(undriven_33), .in2(undriven_2), .in3(undriven_34), .in4(undriven_3),
    .in5(undriven_35), .in6(undriven_4), .in7(undriven_36), .in8(undriven_5), .in9(undriven_37),
    .in10(undriven_6), .in11(undriven_38), .in12(undriven_7), .in13(undriven_39), .in14(undriven_8),
    .in15(undriven_40), .in16(undriven_9), .in17(undriven_41), .in18(undriven_10), .in19(undriven_42),
    .in20(undriven_11), .in21(undriven_43), .in22(undriven_12), .in23(undriven_44), .in24(undriven_13),
    .in25(undriven_45), .in26(undriven_14), .in27(undriven_46), .in28(undriven_15), .in29(undriven_47),
    .in30(undriven_16), .in31(undriven_48), .out(mux0), .sel(Addr[4:0]));
  Multiplexer #(.select(5), .width(16), .enable("false")) multiplexer_2 (
    .in0(undriven_17), .in1(undriven_49), .in2(undriven_18), .in3(undriven_50), .in4(undriven_19),
    .in5(undriven_51), .in6(undriven_20), .in7(undriven_52), .in8(undriven_21), .in9(undriven_53),
    .in10(undriven_22), .in11(undriven_54), .in12(undriven_23), .in13(undriven_55), .in14(undriven_24),
    .in15(undriven_56), .in16(undriven_25), .in17(undriven_57), .in18(undriven_26), .in19(undriven_58),
    .in20(undriven_27), .in21(undriven_59), .in22(undriven_28), .in23(undriven_60), .in24(undriven_29),
    .in25(undriven_61), .in26(undriven_30), .in27(undriven_62), .in28(undriven_31), .in29(undriven_63),
    .in30(undriven_32), .in31(undriven_64), .out(mux1), .sel(Addr[4:0]));
  Multiplexer #(.select(5), .width(16), .enable("false")) multiplexer_3 (
    .in0(undriven_65), .in1(undriven_97), .in2(undriven_66), .in3(undriven_98), .in4(undriven_67),
    .in5(undriven_99), .in6(undriven_68), .in7(undriven_100), .in8(undriven_69), .in9(undriven_101),
    .in10(undriven_70), .in11(undriven_102), .in12(undriven_71), .in13(undriven_103), .in14(undriven_72),
    .in15(undriven_104), .in16(undriven_73), .in17(undriven_105), .in18(undriven_74), .in19(undriven_106),
    .in20(undriven_75), .in21(undriven_107), .in22(undriven_76), .in23(undriven_108), .in24(undriven_77),
    .in25(undriven_109), .in26(undriven_78), .in27(undriven_110), .in28(undriven_79), .in29(undriven_111),
    .in30(undriven_80), .in31(undriven_112), .out(mux2), .sel(Addr[4:0]));
  Multiplexer #(.select(5), .width(16), .enable("false")) multiplexer_4 (
    .in0(undriven_81), .in1(undriven_113), .in2(undriven_82), .in3(undriven_114), .in4(undriven_83),
    .in5(undriven_115), .in6(undriven_84), .in7(undriven_116), .in8(undriven_85), .in9(undriven_117),
    .in10(undriven_86), .in11(undriven_118), .in12(undriven_87), .in13(undriven_119), .in14(undriven_88),
    .in15(undriven_120), .in16(undriven_89), .in17(undriven_121), .in18(undriven_90), .in19(undriven_122),
    .in20(undriven_91), .in21(undriven_123), .in22(undriven_92), .in23(undriven_124), .in24(undriven_93),
    .in25(undriven_125), .in26(undriven_94), .in27(undriven_126), .in28(undriven_95), .in29(undriven_127),
    .in30(undriven_96), .in31(undriven_128), .out(mux3), .sel(Addr[4:0]));
  Multiplexer #(.select(2), .width(16), .enable("false")) multiplexer_5 (
    .in0(mux0), .in1(mux1), .in2(mux2), .in3(mux3), .out(Instr), .sel(Addr[6:5]));
  // Probe on Instr

  // Other names for the same wires on the sheet: sel[1:0] = Addr[6:5]
endmodule
